// Logisim project ALU.circ as structural Verilog: 4 circuits, main circuit main
module main (
  input  [7:0] A,
  input  [7:0] B,
  input  [7:0] in_3
);

  xor xor_1 (in_3[0], A[0], B[0]);
  xor xor_2 (in_3[1], A[1], B[1]);
  xor xor_3 (in_3[2], A[2], B[2]);
  xor xor_4 (in_3[3], A[3], B[3]);
  xor xor_5 (in_3[4], A[4], B[4]);
  xor xor_6 (in_3[5], A[5], B[5]);
  xor xor_7 (in_3[6], A[6], B[6]);
  xor xor_8 (in_3[7], A[7], B[7]);
endmodule

module Add_1bit (
  input  A,
  input  B,
  output Value,
  output Carry
);

  wire not_1_out;

  xor xor_1 (Value, A, B);
  not not_1 (not_1_out, Value);
  and and_1 (Carry, not_1_out, A, B);
endmodule

module Add_8bits (
  input  [7:0] A,
  input  [7:0] B,
  input  [7:0] S,
  output Overflow
);

  wire add_3bit_2_carry_out, add_3bit_3_carry_out, add_3bit_4_carry_out, add_3bit_5_carry_out;

  Add_1bit add_1bit_1 (.A(A[0]), .B(B[0]), .Value(S[0]), .Carry(A[1]));
  Add_3bit add_3bit_1 (.A(A[1]), .B(A[1]), .Carry_In(A[1]), .Value(S[1]), .Carry_Out(A[2]));
  Add_3bit add_3bit_2 (.A(A[2]), .B(A[2]), .Carry_In(A[2]), .Value(S[2]), .Carry_Out(add_3bit_2_carry_out));
  Add_3bit add_3bit_3 (
    .A(A[3]), .B(B[3]), .Carry_In(add_3bit_2_carry_out), .Value(S[3]), .Carry_Out(add_3bit_3_carry_out));
  Add_3bit add_3bit_4 (
    .A(A[4]), .B(B[4]), .Carry_In(add_3bit_3_carry_out), .Value(S[4]), .Carry_Out(add_3bit_4_carry_out));
  Add_3bit add_3bit_5 (
    .A(A[5]), .B(B[5]), .Carry_In(add_3bit_4_carry_out), .Value(S[5]), .Carry_Out(add_3bit_5_carry_out));
  Add_3bit add_3bit_6 (.A(A[6]), .B(B[6]), .Carry_In(add_3bit_5_carry_out), .Value(S[6]), .Carry_Out(A[7]));
  Add_3bit add_3bit_7 (.A(A[7]), .B(A[7]), .Carry_In(A[7]), .Value(S[7]), .Carry_Out(Overflow));

  assign {B[7], B[2:1]} = {A[7], A[2:1]};
endmodule

module Add_3bit (
  input  A,
  input  B,
  input  Carry_In,
  output Value,
  output Carry_Out
);

  wire add_1bit_1_value;

  Add_1bit add_1bit_1 (.A(A), .B(B), .Value(add_1bit_1_value), .Carry(Carry_Out));
  Add_1bit add_1bit_2 (.A(add_1bit_1_value), .B(Carry_In), .Value(Value));  // open: Carry
endmodule
