// Logisim project CyProcessingUnit.circ as structural Verilog
module main (
  input  in_1,
  input  in_2,
  input  in_3,
  output [23:0] out_4,
  output [7:0] Data,
  output [7:0] A,
  output [7:0] B,
  output [7:0] C,
  output [7:0] out_9,
  output [7:0] out_10
);

  wire alu_1_error, decoders_1_p4, registerband_8bit_1_p7;
  wire [3:0] decoder_operation_1_s, decoders_1_p5, decoders_1_p6;
  wire [7:0] decoders_1_p7, fetch_1_b2, fetch_1_c2, ram_instruction_1_b2, ram_instruction_1_c2;

  RAM_data ram_data_1 ();  // open: in_1, out_2
  RAM_Instruction ram_instruction_1 (
    .Memory_Choice(out_4), .WE(in_2), .RE(in_3), .A2(out_9), .B2(ram_instruction_1_b2),
    .C2(ram_instruction_1_c2));
  IP ip_1 (.Kill(in_1), .out_2(out_4));
  Fetch fetch_1 (
    .A1(out_9), .B1(ram_instruction_1_b2), .C1(ram_instruction_1_c2), .A2(out_10), .B2(fetch_1_b2),
    .C2(fetch_1_c2));
  // Decoders decoders_1: pin names not known; wires that end beside it: out_10, fetch_1_b2, fetch_1_c2, decoders_1_p4, decoders_1_p5, decoders_1_p6, decoders_1_p7[3:0], decoders_1_p7[7:4]
  // RegisterBand_8bit registerband_8bit_1: pin names not known; wires that end beside it: C, decoders_1_p6[2:0], decoders_1_p4, decoders_1_p5[2:0], A, B, registerband_8bit_1_p7
  Decoder_Operation decoder_operation_1 (.A(decoders_1_p7), .S(decoder_operation_1_s));
  LED led_1 (.in(alu_1_error));
  ALU alu_1 (.A(A), .B(B), .SlctOP(decoder_operation_1_s), .Error(alu_1_error), .C(C));

  assign Data = C;
endmodule

module Decoder_Operation (
  input  [7:0] A,
  output [3:0] S
);

  wire not_2_out, not_3_out, or_1_out, or_2_out, or_3_out, or_4_out, or_5_out, or_6_out;

  not not_1 (S[2], A[4]);
  not not_2 (not_2_out, A[3]);
  not not_3 (not_3_out, A[1]);
  or or_1 (or_1_out, A[4], A[3]);
  or or_2 (or_2_out, S[2], not_2_out);
  or or_3 (or_3_out, S[2], A[1]);
  or or_4 (or_4_out, A[4], not_3_out);
  or or_5 (or_5_out, A[4], A[2]);
  or or_6 (or_6_out, A[2], A[0]);
  and and_1 (S[3], or_1_out, or_2_out);
  and and_2 (S[1], not_2_out, or_3_out, or_4_out);
  and and_3 (S[0], or_5_out, or_6_out);
endmodule

module Fetch (
  input  [7:0] A1,
  input  [7:0] B1,
  input  [7:0] C1,
  output [7:0] A2,
  output [7:0] B2,
  output [7:0] C2
);

  Register_24bit register_24bit_1 (.in_1({C1, B1, A1}), .WE(1'b1), .out_3({C2, B2, A2}));
endmodule

module RAM_Instruction (
  input  [23:0] Memory_Choice,
  input  WE,
  input  RE,
  output [7:0] A2,
  output [7:0] B2,
  output [7:0] C2
);

  wire clock_1_out;

  RAM #(.addrWidth(24), .dataWidth(24)) ram_1 (
    .addr(Memory_Choice), .we(WE), .oe(RE), .clk(clock_1_out), .dout({C2, B2, A2}));  // open: din
  Clock clock_1 (.out(clock_1_out));
endmodule

module RAM_data (
  input  [7:0] in_1,
  output [7:0] out_2
);

  RAM ram_1 (.din(in_1), .dout(out_2));  // open: addr, we, oe, clk
endmodule

module Decoders (
  input  [7:0] A,
  input  [7:0] B,
  input  [7:0] C,
  input  zero,
  output [3:0] Rout,
  output [3:0] Unused,
  output [3:0] Rin2,
  output [3:0] Rin1,
  output [3:0] Operation,
  output [3:0] Type_Op
);

  Register_24bit register_24bit_1 (.in_1({C, B, A}), .WE(1'b1), .out_3({Type_Op, Operation, Rin1, Rin2, Unused, Rout}));
endmodule

module IP (
  input  Kill,
  output [23:0] out_2
);

  wire clock_1_out;
  wire [23:0] register_24bit_1_out_3;

  Register_24bit register_24bit_1 (.in_1(out_2), .out_3(register_24bit_1_out_3));  // open: WE
  Clock clock_1 (.out(clock_1_out));
  Counter #(.max('hffffff), .width(24)) counter_1 (
    .D(register_24bit_1_out_3), .Q(out_2), .clk(clock_1_out), .clr(Kill));  // open: load, count, carry, up
endmodule
